# Fritzing sketch Untitled Sketch 2 (saved by Fritzing 0.9.3b)
breadboards: 1

parts:
  Onderdeel1 = Arduino Uno (Rev3)
  IC1 = H-Bridge [package=THT]  # not connected
  VCC1 = Battery block 9V  # not connected
  R1 = Rotary Potentiometer (Small) [maximum_resistance=100kΩ package=THT]
  M1 = DC Motor  # not connected
  M2 = DC Motor  # not connected
  hc-sr1 = hc-sr04
  hc-sr2 = hc-sr04
  hc-sr3 = hc-sr04
  VCC2 = Battery block 9V

nets:
  N1: Onderdeel1.A5/SCL, R1.wiper
  VCC: Onderdeel1.5V, R1.leg1, hc-sr1.VCC, hc-sr2.VCC, hc-sr3.VCC, VCC2.+
  GND: Onderdeel1.GND, R1.leg2, hc-sr1.GND, hc-sr2.GND, hc-sr3.GND, VCC2.-
